# Fritzing sketch Edited (saved by Fritzing 0.9.10b)
circuit board: 14.2225cm x 8.61013cm
breadboards: 1

parts:
  2_Channel_Relay_for_Pellet_Arm = 2 Channel Power Relay
  Motor_2 = EasyDriver_v44
  Motor_1 = EasyDriver_v44
  M1 = Stepper Motor - Bipolar
  M2 = Stepper Motor - Bipolar
  IR_Lights_Relay = Keyes Relay [package=THT]
  LED1 = LEDs [package=led10mm]
  Servo = Solenoid
  BB = IR break beam 3mm tx [package=THT]  # not connected
  Beam_Breaker = IR break beam 3mm rx [package=THT]
  Switch_1 = Square Pushbutton
  Switch2 = Square Pushbutton
  12_v_Power_supply_goes_through_Stepdown_to_become_9V = Battery block 9V
  Lights_Power_Supply = Battery block 9V
  A1 = Raspberry Pi 5

nets:
  GND: 2_Channel_Relay_for_Pellet_Arm.GND, 2_Channel_Relay_for_Pellet_Arm.K2-NO, Motor_2.GND, Motor_2.MS1, Motor_2.MS2, Motor_1.GND, Motor_1.MS1, Motor_1.MS2, IR_Lights_Relay.ground, Beam_Breaker.pin3, Switch_1.leg1, Switch2.leg1, 12_v_Power_supply_goes_through_Stepdown_to_become_9V.-
  N1: 2_Channel_Relay_for_Pellet_Arm.IN1, A1.GPIO5
  N2: 2_Channel_Relay_for_Pellet_Arm.IN2, A1.GPIO6
  N3: 2_Channel_Relay_for_Pellet_Arm.VCC, 2_Channel_Relay_for_Pellet_Arm.K1-NC, 2_Channel_Relay_for_Pellet_Arm.K2-NC, Motor_2.V+, Motor_1.V+, IR_Lights_Relay.power, Beam_Breaker.pin1, 12_v_Power_supply_goes_through_Stepdown_to_become_9V.+
  N4: 2_Channel_Relay_for_Pellet_Arm.K1-COM, Servo.pin1
  N5: 2_Channel_Relay_for_Pellet_Arm.K2-COM, Servo.pin2
  N6: Motor_2.STEP, A1.GPIO23, A1.3V3
  N7: Motor_2.DIR, A1.GPIO22
  N8: Motor_2.OUT2A, M2.A
  N9: Motor_2.OUT2B, M2.C
  N10: Motor_2.OUT1A, M2.B
  N11: Motor_2.OUT1B, M2.D
  N12: Motor_2.ENABLE, A1.GPIO25, A1.GPIO11
  N13: Motor_1.STEP, A1.GPIO17
  N14: Motor_1.DIR, A1.GPIO27
  N15: Motor_1.OUT2A, M1.A
  N16: Motor_1.OUT2B, M1.C
  N17: Motor_1.OUT1A, M1.B
  N18: Motor_1.OUT1B, M1.D
  N19: Motor_1.ENABLE, A1.GPIO24, A1.GPIO10
  N20: IR_Lights_Relay.C, Lights_Power_Supply.+
  N21: IR_Lights_Relay.NO, LED1.A
  N22: LED1.C, Lights_Power_Supply.-
  N23: Beam_Breaker.pin2, A1.GPIO26
  N24: Switch_1.leg0, A1.GPIO7, A1.ID_SD
  N25: Switch2.leg0, A1.GND, A1.GPIO8

notes:
  9V Power Line

custom parts:
  2 Channel Power Relay: A 2 channel power relay. The module operates at 5V.
  Keyes Relay: The Keyes 5V relay module is suitable for SCM development, home appliance control. It uses a 5V~12V TIL control signal which can control DC / AC signal.
  IR break beam 3mm tx: Infrared break beam Sensor tx module.
  IR break beam 3mm rx: Infrared break beam Sensor rx module.
  Raspberry Pi 5: The RPi5, a faster version of the awesome Raspberry Pi4B ARM Board with 40 pin gpio.
